# Fritzing sketch YellowTruck_0_ReverseEngineering (saved by Fritzing 0.7.11b)
stripboards: 4
perfboards: 1

parts:
  S1 = Pushbutton [package="[THT]"]
  S2 = Pushbutton [package="[THT]"]
  S3 = Toggle Switch [package=THT]
  S4 = Toggle Switch [package=THT]
  LED3 = LED - 3mm [color="White (4500K)" package="3 mm [THT]"]
  LED2 = LED - 3mm [color="Yellow (595nm)" package="3 mm [THT]"]
  LED1 = LED - 3mm [color="Yellow (595nm)" package="3 mm [THT]"]
  LED4 = LED - 3mm [color="White (4500K)" package="3 mm [THT]"]  # not connected
  M1 = DC Motor
  M2 = DC Motor
  M3 = DC Motor  # not connected
  S5 = Toggle Switch [package=THT]  # not connected
  S6 = Toggle Switch [package=THT]  # not connected

nets:
  N1: S1.Pin_1, S1.Pin_2, S1.Pin_3, S1.Pin_4, S2.Pin_1, S2.Pin_2, S2.Pin_3, S2.Pin_4, M2.pin_2
  N2: S3.L1, S4.L2
  N3: S3.L2, S4.L1
  N4: LED3.cathode, LED2.cathode, LED1.cathode, M1.pin_2
  N5: LED3.anode, LED2.anode, LED1.anode, M1.pin_1

notes:
  0 V
  Questo rappresenta il set di 4 stilo AA
  1,5 V
  3 V
  4,5 V
  6 V
  MOTOR 1
  Questo rappresenta uno dei due switch di polarità per gestire il motore 1 e il suo senso di rotazione
  I due interuttori vanno considerati sincroni.
  Quando sono al centro non passa corrente. Quando sono verso l'alto la polarità è mantenuta (il motore gira in senso orario). Quando sono in basso la polarità è invertita (il motore gira in senso antiorario).
  MOTOR 2
  Questo rappresenta uno dei due switch di polarità per gestire il motore 2 e il suo senso di rotazione
  v. sopra ( non ho implementato l circuito)
  Motore Posteriore di trazione
  Motore Argano
  Motore Anteriore di direzione
  Buzzer
  non ho fatto il reverse del buzzer
