# Fritzing sketch YellowTruck_1_L293D (saved by Fritzing 0.7.11b)
stripboards: 1

parts:
  Arduino1 = Arduino
  IC1 = L293D [package=THT]
  Componente1 = Thumb Joystick
  M1 = DC Motor
  M2 = DC Motor
  VCC1 = Battery block 9V

nets:
  GND: Arduino1.GND, IC1.0V, Componente1.GND, VCC1.-
  +5V: Arduino1.D11, Arduino1.+5V, IC1.Enable_1, IC1.+Vmotor, IC1.Enable_2, IC1.+V, Componente1.VCC, VCC1.+
  N1: Arduino1.D10, Arduino1.D3, IC1.In_1, IC1.In_4
  N2: Arduino1.D9, Arduino1.D2, IC1.In_2, IC1.In_3
  N3: Arduino1.A0, Componente1.VERT
  N4: Arduino1.A1, Componente1.HORZ
  N5: IC1.Out_1_(_Controlled_by_Enable_1_), IC1.Out_4_(_Controlled_by_Enable_2_), M1.pin_1, M2.pin_1
  N6: IC1.Out_2_(_Controlled_by_Enable_1_), IC1.Out_3_(_Controlled_by_Enable_2_), M1.pin_2, M2.pin_2

notes:
  Motor 1 speed is controlled in PWM by pin 11
  Motor 2
