# Fritzing sketch YellowTruck_2_74HC595 (saved by Fritzing 0.7.11b)
breadboards: 2

parts:
  Arduino1 = Arduino
  Componente1 = Thumb Joystick
  U1 = 74HC595 [package="DIP16 [THT]"]
  R1 = Resistor [tolerance=±5% resistance=220 package=THT]
  R2 = Resistor [tolerance=±5% resistance=220 package=THT]
  R3 = Resistor [tolerance=±5% resistance=220 package=THT]
  R4 = Resistor [tolerance=±5% resistance=220 package=THT]
  R5 = Resistor [tolerance=±5% resistance=220 package=THT]
  R6 = Resistor [tolerance=±5% resistance=220 package=THT]
  R7 = Resistor [tolerance=±5% resistance=220 package=THT]
  R8 = Resistor [tolerance=±5% resistance=220 package=THT]
  R9 = Resistor [tolerance=±5% resistance=220 package=THT]
  R10 = Resistor [tolerance=±5% resistance=220 package=THT]
  LED1 = LED - 5mm [color="Orange (605nm)" package="5 mm [THT]"]
  LED2 = LED - 5mm [color="Orange (605nm)" package="5 mm [THT]"]
  LED3 = LED - 5mm [color="Orange (605nm)" package="5 mm [THT]"]
  LED4 = LED - 5mm [color="Orange (605nm)" package="5 mm [THT]"]
  LED5 = LED - 5mm [color="Blue (505nm)" package="5 mm [THT]"]
  LED6 = LED - 5mm [color="Blue (505nm)" package="5 mm [THT]"]
  LED7 = LED - 5mm [color="Blue (505nm)" package="5 mm [THT]"]
  LED8 = LED - 5mm [color="Blue (505nm)" package="5 mm [THT]"]
  LED9 = LED - 5mm [color="Red (633nm)" package="5 mm [THT]"]
  LED10 = LED - 5mm [color="Red (633nm)" package="5 mm [THT]"]

nets:
  N1: Arduino1.D12, U1.SH_CP
  N2: Arduino1.D11, U1.DS
  N3: Arduino1.D10, R1.Pin_0
  N4: Arduino1.D8, U1.ST_CP, R2.Pin_0
  VCC: Arduino1.+5V, Arduino1.A0, Componente1.VERT, Componente1.VCC, U1.MR, U1.VCC
  GND: Arduino1.GND, Componente1.GND, U1.GND, U1.OE, LED1.cathode, LED3.cathode, LED4.cathode, LED5.cathode, LED6.cathode, LED7.cathode, LED8.cathode, LED9.cathode, LED10.cathode
  N5: Arduino1.A1, Componente1.HORZ
  N6: Arduino1.A2, Componente1.SEL
  N7: U1.Q1, R9.Pin_0
  N8: U1.Q2, R8.Pin_0
  N9: U1.Q3, R7.Pin_0
  N10: U1.Q4, R6.Pin_0
  N11: U1.Q5, R5.Pin_0
  N12: U1.Q6, R4.Pin_0
  N13: U1.Q7, R3.Pin_0
  N14: U1.Q0, R10.Pin_0
  N15: R1.Pin_1, LED10.anode
  N16: R2.Pin_1, LED9.anode
  N17: R4.Pin_1, LED2.anode
  N18: R5.Pin_1, LED3.anode
  N19: R6.Pin_1, LED4.anode
  N20: R7.Pin_1, LED5.anode
  N21: R8.Pin_1, LED6.anode
  N22: R9.Pin_1, LED7.anode
  N23: R10.Pin_1, LED8.anode
