# Fritzing sketch YellowTruck_3 (saved by Fritzing 0.7.11b)
stripboards: 2

parts:
  Arduino1 = Arduino
  IC1 = L293D [package=THT]
  M1 = DC Motor
  M2 = DC Motor
  VCC1 = Battery block 9V
  IR1 = TSOP312.., 314.. [package=THT]
  VCC2 = Battery  # not connected
  C1 = Electrolytic Capacitor [capacitance=10µF voltage=6.3V package="100 mil [THT, electrolytic]"]
  LED1 = LED - 3mm [color="Red (633nm)" package="3 mm [THT]"]
  R2 = Resistor [tolerance=±5% resistance=220 package=THT]
  R3 = Resistor [tolerance=±5% resistance=100 package=THT]
  R4 = Resistor [tolerance=±5% resistance=220 package=THT]
  LED2 = LED - 3mm [color="Green (555nm)" package="3 mm [THT]"]
  C2 = Electrolytic Capacitor [capacitance=470µF voltage=16V package="100 mil [THT, electrolytic]"]

nets:
  N1: Arduino1.D11, Arduino1.+5V, IC1.Enable_1, IC1.+Vmotor, IC1.Enable_2, IC1.+V, VCC1.+, C1.+, R3.Pin_1, C2.+
  N2: Arduino1.D10, Arduino1.D3, IC1.In_1, IC1.In_4
  N3: Arduino1.D9, Arduino1.D2, IC1.In_2, IC1.In_3
  N4: Arduino1.D7, R2.Pin_1
  N5: Arduino1.D6, R4.Pin_1
  N6: Arduino1.D5, IR1.Data
  GND: Arduino1.GND, IC1.0V, VCC1.-, IR1.GND, C1.-, LED1.cathode, LED2.cathode, C2.-
  N7: IC1.Out_1_(_Controlled_by_Enable_1_), IC1.Out_4_(_Controlled_by_Enable_2_), M1.pin_1, M2.pin_1
  N8: IC1.Out_2_(_Controlled_by_Enable_1_), IC1.Out_3_(_Controlled_by_Enable_2_), M1.pin_2, M2.pin_2
  N9: IR1.Vs, R3.Pin_0
  N10: LED1.anode, R2.Pin_0
  N11: R4.Pin_0, LED2.anode

notes:
  Motor 1 speed is controlled in PWM by pin 11
  Motor 2 direction controll
  Remote IR Reciever TSOP2438 (PIN on sketch do not correspond to real pin)
  Remote used model do not have Part Nb. Remap with your own.
  RED: unkown IR command
  GREEN: known IR command
